// Logisim project Problem03.circ as structural Verilog: 1 circuit, main circuit main
module main (
  input  AND,
  input  in_2,
  input  OR,
  input  in_4,
  input  NOT,
  input  XOR,
  input  in_7,
  input  XNOR,
  input  in_9,
  output out_10,
  output out_11,
  output out_12,
  output out_13
);

  wire nand_1_out, nand_2_out, nand_3_out, nand_5_out, nand_6_out, nand_9_out, nand_10_out, nand_11_out,
       nand_12_out, nand_14_out;

  nand nand_1 (nand_1_out, AND, in_2);
  nand nand_2 (nand_2_out, OR, OR);
  nand nand_3 (nand_3_out, in_4, in_4);
  // NAND_Gate nand_4 has open pins: in0=NOT, in1=NOT, out=open
  nand nand_5 (nand_5_out, XOR, in_7);
  nand nand_6 (nand_6_out, XNOR, in_9);
  nand nand_7 (out_10, nand_1_out, nand_1_out);
  nand nand_8 (out_11, nand_2_out, nand_3_out);
  nand nand_9 (nand_9_out, XOR, nand_5_out);
  nand nand_10 (nand_10_out, nand_5_out, in_7);
  nand nand_11 (nand_11_out, XNOR, nand_6_out);
  nand nand_12 (nand_12_out, nand_6_out, in_9);
  nand nand_13 (out_12, nand_9_out, nand_10_out);
  nand nand_14 (nand_14_out, nand_11_out, nand_12_out);
  nand nand_15 (out_13, nand_14_out, nand_14_out);
endmodule
