// Logisim project Problem04.circ as structural Verilog: 1 circuit, main circuit main
module main (
  input  NOT,
  input  OR,
  input  in_3,
  input  AND,
  input  in_5,
  input  XOR,
  input  in_7,
  output out_8,
  output out_9,
  output out_10,
  output out_11
);

  wire nor_2_out, nor_3_out, nor_4_out, nor_5_out, nor_8_out, nor_9_out, nor_10_out;

  nor nor_1 (out_8, NOT, NOT);
  nor nor_2 (nor_2_out, OR, in_3);
  nor nor_3 (nor_3_out, AND, AND);
  nor nor_4 (nor_4_out, in_5, in_5);
  nor nor_5 (nor_5_out, XOR, in_7);
  nor nor_6 (out_9, nor_2_out, nor_2_out);
  nor nor_7 (out_10, nor_3_out, nor_4_out);
  nor nor_8 (nor_8_out, XOR, nor_5_out);
  nor nor_9 (nor_9_out, nor_5_out, in_7);
  nor nor_10 (nor_10_out, nor_8_out, nor_9_out);
  nor nor_11 (out_11, nor_10_out, nor_10_out);
endmodule
