// Logisim project Problem05.circ as structural Verilog: 1 circuit, main circuit main
module main (
  input  in_1,
  input  in_2,
  input  in_3,
  input  in_4,
  output out_5
);

  wire n7400_1_pin3, n7400_1_pin6, n7400_1_pin8, n7400_1_pin11, n7400_2_pin3, n7400_2_pin6, n7400_2_pin8,
       n7400_2_pin11, n7400_3_pin3, n7400_3_pin6, n7400_3_pin11;

  _7400 #(.ShowInternalStructure("true")) u_7400_1 (
    .pin1(in_1), .pin2(in_2), .pin3(n7400_1_pin3), .pin4(n7400_1_pin3), .pin5(in_2), .pin6(n7400_1_pin6),
    .pin13(in_1), .pin12(n7400_1_pin3), .pin11(n7400_1_pin11), .pin10(n7400_1_pin11), .pin9(n7400_1_pin6),
    .pin8(n7400_1_pin8));
  _7400 #(.ShowInternalStructure("true")) u_7400_2 (
    .pin1(in_3), .pin2(in_4), .pin3(n7400_2_pin3), .pin4(n7400_2_pin3), .pin5(in_4), .pin6(n7400_2_pin6),
    .pin13(in_3), .pin12(n7400_2_pin3), .pin11(n7400_2_pin11), .pin10(n7400_2_pin11), .pin9(n7400_2_pin6),
    .pin8(n7400_2_pin8));
  _7400 #(.ShowInternalStructure("true")) u_7400_3 (
    .pin1(n7400_1_pin8), .pin2(n7400_2_pin8), .pin3(n7400_3_pin3), .pin4(n7400_3_pin3), .pin5(n7400_2_pin8),
    .pin6(n7400_3_pin6), .pin13(n7400_1_pin8), .pin12(n7400_3_pin3), .pin11(n7400_3_pin11),
    .pin10(n7400_3_pin11), .pin9(n7400_3_pin6), .pin8(out_5));
endmodule
