// Logisim project Problem06.circ as structural Verilog: 1 circuit, main circuit main
module main (
  input  X1,
  input  X2,
  input  X0,
  output out_4
);

  wire nand_1_out, nand_2_out, nand_3_out, nand_4_out, nand_5_out, nand_6_out, nand_7_out;

  nand nand_1 (nand_1_out, X1, X1);
  nand nand_2 (nand_2_out, X2, X2);
  nand nand_3 (nand_3_out, nand_1_out, nand_2_out);
  nand nand_4 (nand_4_out, nand_3_out, X0);
  nand nand_5 (nand_5_out, nand_3_out, nand_4_out);
  nand nand_6 (nand_6_out, nand_4_out, X0);
  nand nand_7 (nand_7_out, nand_5_out, nand_6_out);
  nand nand_8 (out_4, nand_7_out, nand_7_out);
endmodule
