// Logisim project Problem02.circ as structural Verilog: 1 circuit, main circuit main
module main (
  input  D,
  input  C,
  input  B,
  input  A
);

  wire and_1_out, and_2_out, and_3_out, and_4_out, and_5_out, and_6_out, and_7_out, and_8_out, and_9_out,
       and_10_out, and_11_out, and_12_out, and_13_out, and_14_out, and_15_out, and_16_out, and_17_out,
       and_18_out, and_19_out, and_20_out, and_21_out, and_22_out, and_23_out, and_24_out, and_25_out,
       and_26_out, and_27_out, and_28_out, and_29_out, and_30_out, and_31_out, and_32_out, and_33_out,
       and_34_out, and_35_out, not_1_out, not_2_out, not_3_out, not_4_out, O_a_out, O_b_out, O_c_out,
       O_d_out, O_e_out, O_f_out, O_g_out;

  not not_1 (not_1_out, D);
  not not_2 (not_2_out, C);
  not not_3 (not_3_out, B);
  not not_4 (not_4_out, A);
  and and_1 (and_1_out, D, not_2_out);
  and and_2 (and_2_out, not_2_out, B);
  and and_3 (and_3_out, not_1_out, C, not_3_out);
  and and_4 (and_4_out, D, A);
  and and_5 (and_5_out, B, not_4_out);
  and and_6 (and_6_out, D, not_2_out);
  and and_7 (and_7_out, D, B);
  and and_8 (and_8_out, not_1_out, C, not_3_out);
  and and_9 (and_9_out, C, not_4_out);
  and and_10 (and_10_out, not_3_out, not_4_out);
  and and_11 (and_11_out, D, C);
  and and_12 (and_12_out, D, B);
  and and_13 (and_13_out, not_2_out, not_4_out);
  and and_14 (and_14_out, B, not_4_out);
  and and_15 (and_15_out, D, not_3_out);
  and and_16 (and_16_out, not_2_out, B, A);
  and and_17 (and_17_out, C, not_3_out, A);
  and and_18 (and_18_out, not_1_out, not_2_out, not_4_out);
  and and_19 (and_19_out, C, B, not_4_out);
  and and_20 (and_20_out, not_1_out, C);
  and and_21 (and_21_out, D, not_2_out);
  and and_22 (and_22_out, not_1_out, not_3_out);
  and and_23 (and_23_out, not_1_out, A);
  and and_24 (and_24_out, not_3_out, A);
  and and_25 (and_25_out, not_1_out, B, A);
  and and_26 (and_26_out, D, not_3_out, A);
  and and_27 (and_27_out, not_1_out, not_3_out, not_4_out);
  and and_28 (and_28_out, not_1_out, not_2_out);
  and and_29 (and_29_out, not_2_out, not_4_out);
  and and_30 (and_30_out, D, not_2_out, not_3_out);
  and and_31 (and_31_out, not_1_out, C, A);
  and and_32 (and_32_out, D, not_3_out, not_4_out);
  and and_33 (and_33_out, not_1_out, B);
  and and_34 (and_34_out, C, B);
  and and_35 (and_35_out, not_2_out, not_4_out);
  nor O_g (O_g_out, and_1_out, and_2_out, and_3_out, and_4_out, and_5_out);
  nor O_f (O_f_out, and_6_out, and_7_out, and_8_out, and_9_out, and_10_out);
  nor O_e (O_e_out, and_11_out, and_12_out, and_13_out, and_14_out);
  nor O_d (O_d_out, and_15_out, and_16_out, and_17_out, and_18_out, and_19_out);
  nor O_c (O_c_out, and_20_out, and_21_out, and_22_out, and_23_out, and_24_out);
  nor O_b (O_b_out, and_25_out, and_26_out, and_27_out, and_28_out, and_29_out);
  nor O_a (O_a_out, and_30_out, and_31_out, and_32_out, and_33_out, and_34_out, and_35_out);
  _7_Segment_Display #(.active("false")) u_7_segment_display_1 (
    .g(O_g_out), .f(O_f_out), .a(O_a_out), .b(O_b_out), .e(O_e_out), .d(O_d_out), .c(O_c_out));  // open: dp
endmodule
