// Logisim project Problem03.circ as structural Verilog: 1 circuit, main circuit main
module main (
  input  X2,
  input  X1,
  input  X0,
  input  I0,
  output Y1,
  output Y0,
  output V
);

  wire and_1_out, not_1_out;

  not not_1 (not_1_out, X1);
  and and_1 (and_1_out, X0, not_1_out);
  or or_1 (V, X2, X1, X0, I0);
  or or_2 (Y1, X2, X1);
  or or_3 (Y0, X2, and_1_out);
endmodule
