// Logisim project Problem04.circ as structural Verilog: 1 circuit, main circuit main
module main (
  input  [3:0] in_1
);

  wire decoder_1_out0, decoder_1_out1, decoder_1_out2, decoder_1_out3;

  Decoder #(.enable("false"), .select(2)) decoder_1 (
    .out0(decoder_1_out0), .out1(decoder_1_out1), .out2(decoder_1_out2), .out3(decoder_1_out3),
    .sel(in_1[3:2]));
  Decoder #(.select(2)) decoder_2 (.sel(in_1[1:0]), .en(decoder_1_out0));  // open: out0, out1, out2, out3
  Decoder #(.select(2)) decoder_3 (.sel(in_1[1:0]), .en(decoder_1_out1));  // open: out0, out1, out2, out3
  Decoder #(.select(2)) decoder_4 (.sel(in_1[1:0]), .en(decoder_1_out2));  // open: out0, out1, out2, out3
  Decoder #(.select(2)) decoder_5 (.sel(in_1[1:0]), .en(decoder_1_out3));  // open: out0, out1, out2, out3
endmodule
