// Logisim project Problem05.circ as structural Verilog: 2 circuits, main circuit main
module main (
  input  X0,
  input  X1,
  input  X2,
  input  X3,
  input  S1,
  input  S0,
  output Q
);

  wire multiplexer_1_out, multiplexer_2_out;

  Multiplexer multiplexer_1 (.in0(X0), .in1(X1), .out(multiplexer_1_out), .sel(S0));
  Multiplexer multiplexer_2 (.in0(X2), .in1(X3), .out(multiplexer_2_out), .sel(S0));
  Multiplexer multiplexer_3 (.in0(multiplexer_1_out), .in1(multiplexer_2_out), .out(Q), .sel(S1));
endmodule

module test (
  input  Q2,
  input  Q1,
  input  Q0,
  output J2,
  output K2,
  output J1,
  output K1,
  output J0,
  output K0
);


  assign J0 = 1'b0;
  assign J1 = 1'b0;
  assign J2 = 1'b0;
  assign K0 = 1'b0;
  assign K1 = 1'b0;
  assign K2 = Q0;
endmodule
