// Logisim project Problem06.circ as structural Verilog: 1 circuit, main circuit main
module main (
  input  X0,
  input  X1,
  input  X2,
  input  X,
  input  X3,
  input  Enable,
  input  S1,
  input  S0,
  input  in_9,
  input  in_10,
  input  in_11,
  input  in_12,
  input  in_13,
  input  in_14,
  input  in_15,
  input  in_16,
  input  in_17,
  input  in_18,
  input  in_19,
  input  in_20,
  input  in_21,
  input  in_22,
  input  in_23,
  input  in_24,
  input  in_25,
  input  in_26,
  input  in_27,
  input  in_28,
  input  in_29,
  input  in_30,
  output Y0,
  output Y1,
  output Q,
  output Y2,
  output Y3,
  output out_36,
  output out_37,
  output out_38,
  output out_39,
  output out_40,
  output out_41,
  output out_42,
  output out_43,
  output out_44
);

  wire and_1_out, and_2_out, and_3_out, and_4_out, and_5_out, and_6_out, and_7_out, and_8_out, and_9_out,
       and_10_out, and_11_out, and_12_out, not_1_out, not_2_out, not_3_out, not_4_out, not_5_out, not_6_out,
       not_7_out, not_8_out, not_9_out, not_10_out, not_11_out, not_12_out, not_13_out, not_14_out, or_2_out,
       or_3_out;

  not not_1 (not_1_out, S1);
  not not_2 (not_2_out, in_16);
  not not_3 (not_3_out, in_25);
  not not_4 (not_4_out, in_26);
  not not_5 (not_5_out, S0);
  not not_6 (not_6_out, in_17);
  not not_7 (not_7_out, in_27);
  and and_1 (and_1_out, Enable, X0, not_1_out, not_5_out);
  and and_2 (and_2_out, Enable, X1, not_1_out, S0);
  and and_3 (and_3_out, Enable, X2, S1, not_5_out);
  and and_4 (and_4_out, Enable, X3, S1, S0);
  and and_5 (and_5_out, not_3_out, in_12, not_2_out, not_6_out);
  and and_6 (and_6_out, not_3_out, in_13, not_2_out, in_17);
  and and_7 (and_7_out, not_3_out, in_14, in_16, not_6_out);
  and and_8 (and_8_out, not_3_out, in_15, in_16, in_17);
  and and_9 (and_9_out, in_25, in_21, not_4_out, not_7_out);
  and and_10 (and_10_out, in_25, in_22, not_4_out, in_27);
  and and_11 (and_11_out, in_25, in_23, in_26, not_7_out);
  and and_12 (and_12_out, in_25, in_24, in_26, in_27);
  or or_1 (Q, and_1_out, and_2_out, and_3_out, and_4_out);
  or or_2 (or_2_out, and_5_out, and_6_out, and_7_out, and_8_out);
  or or_3 (or_3_out, and_9_out, and_10_out, and_11_out, and_12_out);
  or or_4 (out_40, or_2_out, or_3_out);
  not not_8 (not_8_out, in_10);
  not not_9 (not_9_out, in_28);
  not not_10 (not_10_out, in_11);
  not not_11 (not_11_out, in_18);
  not not_12 (not_12_out, in_19);
  not not_13 (not_13_out, in_29);
  not not_14 (not_14_out, in_30);
  and and_13 (Y0, in_9, X, in_10, in_11);
  and and_14 (Y1, in_9, X, not_8_out, in_11);
  and and_15 (Y2, in_9, X, in_10, not_10_out);
  and and_16 (Y3, in_9, X, not_8_out, not_10_out);
  and and_17 (out_36, not_9_out, in_20, in_18, in_19);
  and and_18 (out_37, not_9_out, in_20, not_11_out, in_19);
  and and_19 (out_38, not_9_out, in_20, in_18, not_12_out);
  and and_20 (out_39, not_9_out, in_20, not_11_out, not_12_out);
  and and_21 (out_41, in_28, in_20, in_29, in_30);
  and and_22 (out_42, in_28, in_20, not_13_out, in_30);
  and and_23 (out_43, in_28, in_20, in_29, not_14_out);
  and and_24 (out_44, in_28, in_20, not_13_out, not_14_out);

  // Notes on the sheet:
  //   4:1 Multiplexer
  //   8:1 Multiplexer
  //   1:4 Demultiplexer
  //   1:8 Demultiplexer
endmodule
