// Logisim project Problem07.circ as structural Verilog: 1 circuit, main circuit main
module main (
  input  C,
  input  A_a,
  input  B,
  output Y_a,
  output Y_b
);

  wire n74153_1_pin3, n74153_1_pin5, n74153_1_pin6, n74153_1_pin10, n74153_1_pin12, n74153_1_pin13;

  _74153 #(.ShowInternalStructure("true")) u_74153_1 (
    .pin2(B), .pin3(n74153_1_pin3), .pin5(n74153_1_pin5), .pin6(n74153_1_pin6), .pin7(Y_b), .pin14(C),
    .pin13(n74153_1_pin13), .pin12(n74153_1_pin12), .pin10(n74153_1_pin10), .pin9(Y_a));  // open: pin1, pin4, pin15, pin11
  not not_1 (n74153_1_pin10, A_a);
  // also tied to VCC on the sheet: {n74153_1_pin3, n74153_1_pin13, n74153_1_pin12, n74153_1_pin5, n74153_1_pin6}
endmodule
