// Logisim project ExtraProblem.circ as structural Verilog: 1 circuit, main circuit main
module main (
  input  [3:0] A,
  input  [3:0] B,
  input  Cin,
  output [3:0] out_4
);

  wire [3:0] plarom_1_p2;
  wire [7:0] G0_out;

  and G3 (G0_out[3], A[3], B[3]);
  and G2 (G0_out[2], A[2], B[2]);
  and G1 (G0_out[1], A[1], B[1]);
  and G0 (G0_out[0], A[0], B[0]);
  xor P0 (G0_out[4], A[0], B[0]);
  xor P1 (G0_out[5], A[1], B[1]);
  xor P2 (G0_out[6], A[2], B[2]);
  xor P3 (G0_out[7], A[3], B[3]);
  // PlaRom #(.Contents("2 0*3 2 0*12 2 2 0 0 2 2 0*7 2 0*4 2 0*7 2 0 2 0 2*3 0*6 2 2 0*4 2 0 0 2 0*4 2 0*7 2 0 0 2*5 0*5 2*3 0*4 2 0 2 2 0*4 2 0 0 2 0*4 2 0*7 2 0*3 0*3 1 0*3 1 0 0 1 0*3 1 0*3 1 0 0 1 0*3 1 0*3 1 0*3 1 0 0 1 0*3 1 0*3 1 0*3 1 0*3 1 0*3"), .\and (14)) plarom_1: pin names not known; wires that end beside it: {Cin, G0_out}, plarom_1_p2
  xor S3 (out_4[3], G0_out[7], plarom_1_p2[3]);
  xor S2 (out_4[2], G0_out[6], plarom_1_p2[2]);
  xor S1 (out_4[1], G0_out[5], plarom_1_p2[1]);
  xor S0 (out_4[0], G0_out[4], plarom_1_p2[0]);
endmodule
