// Logisim project Problem01.circ as structural Verilog: 2 circuits, main circuit main
module main (
  input  [7:0] A,
  input  [7:0] B,
  output Cout,
  output [7:0] S
);

  wire fulladder_1_cout, fulladder_2_cout, fulladder_3_cout, fulladder_4_cout, fulladder_5_cout,
       fulladder_6_cout, fulladder_7_cout, not_1_out, not_2_out, not_3_out, not_4_out, not_5_out, not_6_out,
       not_7_out, not_8_out;

  not not_1 (not_1_out, B[0]);
  FullAdder fulladder_1 (.A(A[0]), .B(not_1_out), .Cin(1'b1), .Cout(fulladder_1_cout), .S(S[0]));
  not not_2 (not_2_out, B[1]);
  FullAdder fulladder_2 (.A(A[1]), .B(not_2_out), .Cin(fulladder_1_cout), .Cout(fulladder_2_cout), .S(S[1]));
  not not_3 (not_3_out, B[2]);
  FullAdder fulladder_3 (.A(A[2]), .B(not_3_out), .Cin(fulladder_2_cout), .Cout(fulladder_3_cout), .S(S[2]));
  not not_4 (not_4_out, B[3]);
  FullAdder fulladder_4 (.A(A[3]), .B(not_4_out), .Cin(fulladder_3_cout), .Cout(fulladder_4_cout), .S(S[3]));
  not not_5 (not_5_out, B[4]);
  FullAdder fulladder_5 (.A(A[4]), .B(not_5_out), .Cin(fulladder_4_cout), .Cout(fulladder_5_cout), .S(S[4]));
  not not_6 (not_6_out, B[5]);
  FullAdder fulladder_6 (.A(A[5]), .B(not_6_out), .Cin(fulladder_5_cout), .Cout(fulladder_6_cout), .S(S[5]));
  not not_7 (not_7_out, B[6]);
  FullAdder fulladder_7 (.A(A[6]), .B(not_7_out), .Cin(fulladder_6_cout), .Cout(fulladder_7_cout), .S(S[6]));
  not not_8 (not_8_out, B[7]);
  FullAdder fulladder_8 (.A(A[7]), .B(not_8_out), .Cin(fulladder_7_cout), .Cout(Cout), .S(S[7]));
endmodule

module FullAdder (
  input  A,
  input  B,
  input  Cin,
  output Cout,
  output S
);

  wire and_1_out, and_2_out, xor_1_out;

  xor xor_1 (xor_1_out, A, B);
  xor xor_2 (S, Cin, xor_1_out);
  and and_1 (and_1_out, B, A);
  and and_2 (and_2_out, xor_1_out, Cin);
  or or_1 (Cout, and_1_out, and_2_out);
endmodule
