// Logisim project Problem02.circ as structural Verilog: 2 circuits, main circuit main
module main (
  input  [3:0] A,
  input  [3:0] B,
  output Cout,
  output [3:0] S
);

  wire fulladder_1_cout, fulladder_2_cout, fulladder_3_cout, not_1_out, not_2_out, not_3_out, not_4_out;

  not not_1 (not_1_out, B[0]);
  FullAdder fulladder_1 (.A(A[0]), .B(not_1_out), .Cin(1'b1), .Cout(fulladder_1_cout), .S(S[0]));
  not not_2 (not_2_out, B[1]);
  FullAdder fulladder_2 (.A(A[1]), .B(not_2_out), .Cin(fulladder_1_cout), .Cout(fulladder_2_cout), .S(S[1]));
  not not_3 (not_3_out, B[2]);
  FullAdder fulladder_3 (.A(A[2]), .B(not_3_out), .Cin(fulladder_2_cout), .Cout(fulladder_3_cout), .S(S[2]));
  not not_4 (not_4_out, B[3]);
  FullAdder fulladder_4 (.A(A[3]), .B(not_4_out), .Cin(fulladder_3_cout), .Cout(Cout), .S(S[3]));
endmodule

module FullAdder (
  input  A,
  input  B,
  input  Cin,
  output Cout,
  output S
);

  wire and_1_out, and_2_out, xor_1_out;

  xor xor_1 (xor_1_out, A, B);
  xor xor_2 (S, Cin, xor_1_out);
  and and_1 (and_1_out, B, A);
  and and_2 (and_2_out, xor_1_out, Cin);
  or or_1 (Cout, and_1_out, and_2_out);
endmodule
