// Logisim project Problem03.circ as structural Verilog: 2 circuits, main circuit main
module main (
  input  [3:0] A,
  input  [3:0] B,
  input  C,
  output [3:0] S
);

  wire fulladder_1_cout, fulladder_2_cout, fulladder_4_cout, fulladder_5_cout, xor_1_out, xor_2_out,
       xor_3_out, xor_4_out;

  xor xor_1 (xor_1_out, C, B[0]);
  FullAdder fulladder_1 (.A(A[0]), .B(xor_1_out), .Cin(C), .Cout(fulladder_1_cout), .S(S[0]));
  xor xor_2 (xor_2_out, C, B[1]);
  FullAdder fulladder_2 (.A(A[1]), .B(xor_2_out), .Cin(fulladder_1_cout), .Cout(fulladder_2_cout), .S(S[1]));
  FullAdder fulladder_3 (.A(A[1]), .B(xor_2_out), .Cin(fulladder_1_cout), .Cout(fulladder_2_cout), .S(S[1]));
  xor xor_3 (xor_3_out, C, B[2]);
  FullAdder fulladder_4 (.A(A[2]), .B(xor_3_out), .Cin(fulladder_2_cout), .Cout(fulladder_4_cout), .S(S[2]));
  xor xor_4 (xor_4_out, C, B[3]);
  FullAdder fulladder_5 (.A(A[3]), .B(xor_4_out), .Cin(fulladder_4_cout), .Cout(fulladder_5_cout), .S(S[3]));
  // XOR_Gate Overflow has open pins: in0=fulladder_4_cout, in1=fulladder_5_cout, out=open
endmodule

module FullAdder (
  input  A,
  input  B,
  input  Cin,
  output Cout,
  output S
);

  wire and_1_out, and_2_out, xor_1_out;

  xor xor_1 (xor_1_out, A, B);
  xor xor_2 (S, Cin, xor_1_out);
  and and_1 (and_1_out, B, A);
  and and_2 (and_2_out, xor_1_out, Cin);
  or or_1 (Cout, and_1_out, and_2_out);
endmodule
