// Logisim project Problem04.circ as structural Verilog: 1 circuit, main circuit main
module main (
  input  x0,
  input  y0,
  input  x1,
  input  y1,
  input  x2,
  input  y2,
  input  x3,
  input  y3,
  input  c0,
  output c4,
  output S0,
  output P0,
  output G0,
  output S1,
  output P1,
  output G1,
  output S2,
  output P2,
  output G2,
  output S3,
  output P3,
  output G3
);

  wire and_1_out, and_3_out, and_5_out, and_6_out, and_8_out, and_9_out, and_10_out, and_11_out, and_12_out,
       and_14_out, c1_out, c2_out, c3_out;

  xor xor_1 (P0, x0, y0);
  xor xor_2 (S0, c0, P0);
  and and_1 (and_1_out, c0, P0);
  and and_2 (G0, x0, y0);
  or c1 (c1_out, and_1_out, G0);
  xor xor_3 (P1, x1, y1);
  xor xor_4 (S1, c1_out, P1);
  and and_3 (and_3_out, and_1_out, P1);
  and and_4 (G1, x1, y1);
  and and_5 (and_5_out, G0, P1);
  or c2 (c2_out, and_3_out, and_5_out, G1);
  xor xor_5 (P2, x2, y2);
  xor xor_6 (S2, c2_out, P2);
  and and_6 (and_6_out, and_3_out, P2);
  and and_7 (G2, x2, y2);
  and and_8 (and_8_out, and_5_out, P2);
  and and_9 (and_9_out, G1, P2);
  xor xor_7 (P3, x3, y3);
  xor xor_8 (S3, c3_out, P3);
  or c3 (c3_out, G2, and_9_out, and_8_out, and_6_out);
  and and_10 (and_10_out, and_6_out, P3);
  and and_11 (and_11_out, and_8_out, P3);
  and and_12 (and_12_out, and_9_out, P3);
  and and_13 (G3, x3, y3);
  and and_14 (and_14_out, G2, P3);
  or or_1 (c4, G3, and_14_out, and_12_out, and_11_out, and_10_out);
endmodule
