// Logisim project Problem05.circ as structural Verilog: 2 circuits, main circuit main
module main (
  input  [3:0] A,
  input  [3:0] B,
  output [3:0] BCD_Sum,
  output BCD_Cout
);

  wire adder_1_cout, and_1_out, and_2_out;
  wire [3:0] adder_1_out;

  Adder #(.width(4)) adder_1 (.a(A), .b(B), .out(adder_1_out), .cin(1'b0), .cout(adder_1_cout));
  and and_1 (and_1_out, adder_1_out[1], adder_1_out[3]);
  and and_2 (and_2_out, adder_1_out[2], adder_1_out[3]);
  or or_1 (BCD_Cout, and_1_out, and_2_out, adder_1_cout);
  Adder #(.width(4)) adder_2 (
    .a(adder_1_out), .b({1'b0, {2{BCD_Cout}}, 1'b0}), .out(BCD_Sum), .cin(1'b0));  // open: cout

  // Notes on the sheet:
  //   Is exceed 9
endmodule

module test (
  input  Q2,
  input  Q1,
  input  Q0,
  output J2,
  output K2,
  output J1,
  output K1,
  output J0,
  output K0
);


  assign J0 = 1'b0;
  assign J1 = 1'b0;
  assign J2 = 1'b0;
  assign K0 = 1'b0;
  assign K1 = 1'b0;
  assign K2 = Q0;
endmodule
