// Logisim project Problem06.circ as structural Verilog: 1 circuit, main circuit main
module main (
  input  [7:0] A,
  input  [7:0] B,
  input  Cin,
  output Cout,
  output [7:0] out_5
);

  wire n74181_1_p14, n74181_1_p17, n74181_2_p13, n74181_2_p14, n74181_2_p16;
  wire [7:0] n74181_1_p16, not_1_out, not_2_out;

  assign not_1_out = ~A;  // NOT_Gate not_1, 8 bits wide
  assign not_2_out = ~B;  // NOT_Gate not_2, 8 bits wide
  // _74181 #(.ShowInternalStructure("true")) 74181_1: pin names not known; wires that end beside it: not_2_out[0], not_1_out[1], not_1_out[0], not_2_out[1], 1'b1, not_1_out[2], 1'b0, not_2_out[2], 1'b0, not_1_out[3], 1'b1, not_2_out[3], Cin, n74181_1_p14, 1'b0, n74181_1_p16[0], n74181_1_p17, n74181_1_p16[1], n74181_1_p16[2], n74181_1_p16[3]
  // _74181 #(.ShowInternalStructure("true")) 74181_2: pin names not known; wires that end beside it: not_2_out[4], not_1_out[5], not_1_out[4], not_2_out[5], 1'b1, not_1_out[6], 1'b0, not_2_out[6], 1'b0, not_1_out[7], 1'b1, not_2_out[7], n74181_2_p13, n74181_2_p14, n74181_1_p16[4], n74181_2_p16, n74181_1_p16[5], n74181_1_p16[6], n74181_1_p16[7]
  _74182 #(.ShowInternalStructure("true")) u_74182_1 (
    .pin1(n74181_2_p14), .pin2(n74181_2_p16), .pin3(n74181_1_p14), .pin4(n74181_1_p17), .pin13(Cin),
    .pin12(n74181_2_p13), .pin11(Cout));  // open: pin5, pin6, pin7, pin15, pin14, pin10, pin9
  assign out_5 = ~n74181_1_p16;  // NOT_Gate not_3, 8 bits wide
endmodule
