// Logisim project Problem01.circ as structural Verilog: 2 circuits, main circuit main
module main (
  input  Sb,
  output Z
);

  wire and_1_out, and_2_out, clock_1_out, d_ff_1_q, d_ff_2_q, not_1_out, not_2_out, or_1_out;

  Clock clock_1 (.out(clock_1_out));
  D_Flip_Flop d_ff_1 (.D(or_1_out), .clk(clock_1_out), .Q(d_ff_1_q));  // open: Qn, preset, reset
  and and_1 (and_1_out, not_1_out, d_ff_2_q);
  not not_1 (not_1_out, Sb);
  or or_1 (or_1_out, and_1_out, and_2_out);
  D_Flip_Flop d_ff_2 (.D(Sb), .clk(clock_1_out), .Q(d_ff_2_q));  // open: Qn, preset, reset
  and and_2 (and_2_out, Sb, d_ff_1_q, not_2_out);
  not not_2 (not_2_out, d_ff_2_q);
  and and_3 (Z, d_ff_2_q, d_ff_1_q);
endmodule

module FullAdder (
  input  A,
  input  B,
  input  Cin,
  output Cout,
  output S
);

  wire and_1_out, and_2_out, xor_1_out;

  xor xor_1 (xor_1_out, A, B);
  xor xor_2 (S, Cin, xor_1_out);
  and and_1 (and_1_out, B, A);
  and and_2 (and_2_out, xor_1_out, Cin);
  or or_1 (Cout, and_1_out, and_2_out);
endmodule
