// Logisim project Problem03.circ as structural Verilog: 2 circuits, main circuit main
module main (
  input  [3:0] BCD,
  input  Reset
);

  wire and_1_out, and_2_out, and_3_out, and_4_out, and_5_out, Clk_out, d_ff_1_q, d_ff_1_qn, d_ff_2_q,
       d_ff_2_qn, Is1_out, Is3_out, Is4_out, not_1_out, not_2_out, not_3_out, not_4_out, not_5_out,
       not_6_out, not_7_out, not_8_out, not_9_out, or_1_out, or_2_out, S0_out, S1_out;

  or or_1 (or_1_out, and_1_out, and_2_out);
  or or_2 (or_2_out, and_3_out, and_4_out);
  Clock Clk (.out(Clk_out));
  and and_1 (and_1_out, not_8_out, d_ff_2_qn, d_ff_1_q);
  and and_2 (and_2_out, S0_out, not_8_out, d_ff_1_qn);
  and and_3 (and_3_out, not_9_out, S1_out, d_ff_2_q, d_ff_1_qn);
  and and_4 (and_4_out, not_9_out, not_8_out, d_ff_2_qn, d_ff_1_q);
  D_Flip_Flop d_ff_1 (.D(or_2_out), .clk(Clk_out), .Q(d_ff_1_q), .Qn(d_ff_1_qn), .reset(Reset));  // open: preset
  not not_1 (not_1_out, BCD[0]);
  not not_2 (not_2_out, BCD[1]);
  not not_3 (not_3_out, BCD[2]);
  not not_4 (not_4_out, BCD[3]);
  D_Flip_Flop d_ff_2 (.D(or_1_out), .clk(Clk_out), .Q(d_ff_2_q), .Qn(d_ff_2_qn), .reset(Reset));  // open: preset
  and Is1 (Is1_out, BCD[0], not_2_out, not_3_out, not_4_out);
  and Is3 (Is3_out, BCD[0], BCD[1], not_3_out, not_4_out);
  and Is4 (Is4_out, not_1_out, not_2_out, BCD[2], not_4_out);
  not not_5 (not_5_out, Is1_out);
  not not_6 (not_6_out, Is3_out);
  not not_7 (not_7_out, Is4_out);
  and and_5 (and_5_out, d_ff_2_q, d_ff_1_q);
  and S1 (S1_out, not_5_out, not_6_out);
  and S0 (S0_out, not_5_out, not_7_out);
  LED Z (.in(and_5_out));
  not not_8 (not_8_out, S1_out);
  not not_9 (not_9_out, S0_out);
endmodule

module FullAdder (
  input  A,
  input  B,
  input  Cin,
  output Cout,
  output S
);

  wire and_1_out, and_2_out, xor_1_out;

  xor xor_1 (xor_1_out, A, B);
  xor xor_2 (S, Cin, xor_1_out);
  and and_1 (and_1_out, B, A);
  and and_2 (and_2_out, xor_1_out, Cin);
  or or_1 (Cout, and_1_out, and_2_out);
endmodule
