// Logisim project Problem04.circ as structural Verilog: 1 circuit, main circuit main
module main (
  input  [3:0] BCD,
  input  Reset
);

  wire and_1_out, and_2_out, and_3_out, and_4_out, Clk_out, d_ff_1_q, d_ff_2_q, d_ff_2_qn, Is0_out, Is2_out,
       Is5_out, not_1_out, not_2_out, not_3_out, not_4_out, not_5_out, not_6_out, not_7_out, not_8_out,
       not_9_out, or_1_out, S0_out, S1_out;

  or or_1 (or_1_out, and_2_out, and_3_out);
  Clock Clk (.out(Clk_out));
  and and_1 (and_1_out, not_8_out, S0_out);
  and and_2 (and_2_out, not_9_out, not_8_out, d_ff_2_q);
  and and_3 (and_3_out, S0_out, not_8_out, d_ff_2_qn, d_ff_1_q);
  D_Flip_Flop d_ff_1 (.D(or_1_out), .clk(Clk_out), .Q(d_ff_1_q), .reset(Reset));  // open: Qn, preset
  not not_1 (not_1_out, BCD[0]);
  not not_2 (not_2_out, BCD[1]);
  not not_3 (not_3_out, BCD[2]);
  not not_4 (not_4_out, BCD[3]);
  D_Flip_Flop d_ff_2 (.D(and_1_out), .clk(Clk_out), .Q(d_ff_2_q), .Qn(d_ff_2_qn), .reset(Reset));  // open: preset
  and Is0 (Is0_out, not_1_out, not_2_out, not_3_out, not_4_out);
  and Is2 (Is2_out, not_1_out, BCD[1], not_3_out, not_4_out);
  and Is5 (Is5_out, BCD[0], not_2_out, BCD[2], not_4_out);
  not not_5 (not_5_out, Is0_out);
  not not_6 (not_6_out, Is2_out);
  not not_7 (not_7_out, Is5_out);
  and and_4 (and_4_out, S1_out, not_9_out, d_ff_2_q, d_ff_1_q);
  and S1 (S1_out, not_5_out, not_6_out);
  and S0 (S0_out, not_5_out, not_7_out);
  LED Z (.in(and_4_out));
  not not_8 (not_8_out, S1_out);
  not not_9 (not_9_out, S0_out);
endmodule
